# Fritzing sketch Rainbow Racer (saved by Fritzing 0.9.3b)
breadboards: 1

parts:
  SparkFun_micro_bit_Breakout = SparkFun micro:bit Breakout [part_number=BOB-13988]
  Micro_bit1 = Microbit  # not connected
  Blue = Pushbutton [package="[THT]"]
  Red = Pushbutton [package="[THT]"]
  Yellow = Pushbutton [package="[THT]"]
  Green = Pushbutton [package="[THT]"]
  R1-Blue = Resistor [tolerance=±5% resistance=10k package="0603 [SMD]"]
  R2-Red = Resistor [tolerance=±5% resistance=10k package="0603 [SMD]"]
  R3-Yellow = Resistor [tolerance=±5% resistance=10k package="0603 [SMD]"]
  R4-Green = Resistor [tolerance=±5% resistance=10k package="0603 [SMD]"]

nets:
  N1: SparkFun_micro_bit_Breakout.8, Green.Pin_1, Green.Pin_2, R4-Green.Pin_0
  N2: SparkFun_micro_bit_Breakout.12, Yellow.Pin_1, Yellow.Pin_2, R3-Yellow.Pin_0
  N3: SparkFun_micro_bit_Breakout.13, Red.Pin_1, Red.Pin_2, R2-Red.Pin_0
  N4: SparkFun_micro_bit_Breakout.16, Blue.Pin_1, Blue.Pin_2, R1-Blue.Pin_0
  N5: Blue.Pin_3, Blue.Pin_4, Red.Pin_3, Red.Pin_4, Yellow.Pin_3, Yellow.Pin_4, Green.Pin_3, Green.Pin_4
  N6: R1-Blue.Pin_1, R2-Red.Pin_1, R3-Yellow.Pin_1, R4-Green.Pin_1

custom parts:
  SparkFun micro:bit Breakout: The micro:bit breakout is a board that connects to the BBC micro:bit and expands the capabilities of the development platform by providing access to more pins and allowing for connections to the I2C and SPI buses. This breakout board for the micro:bit’s edge connector allows intermediate and advanced users to connect the micro:bit to breadboards and other sensors, motors, LEDs, and more! The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
  Microbit: BBC Microbit Fritzing part
  Pushbutton: A generic pushbutton.
  Pushbutton: A generic pushbutton.
  Pushbutton: A generic pushbutton.
  Pushbutton: A generic pushbutton.
